# Fritzing sketch Untitled Sketch 3 (saved by Fritzing 0.9.3b)
breadboards: 1

parts:
  Part1 = Arduino Mega 2560 (Rev3)
  RHT1 = Humidity and Temperature Sensor RHT03
  hc-sr1 = hc-sr04
  M1 = Stepper Motor - Bipolar
  M2 = DC Motor
  U1 = RELAY-2 [package=relay-g5v]
  Part2 = Breadboard Power Supply Board SMD
  LCD1 = LCD screen
  J1 = Basic Servo
  BAT1 = BC9VPC [package=bc9vpc]
  Power_plug1 = Power plug

nets:
  N1: Part1.D21/SCL, LCD1.VDD, LCD1.V0
  N2: Part1.D20/SDA, LCD1.VSS
  N3: Part1.D13_PWM, hc-sr1.Trig
  N4: Part1.D12_PWM, hc-sr1.Echo
  N5: Part1.D11_PWM, M1.A
  N6: Part1.D10_PWM, M1.C
  N7: Part1.D9_PWM, M1.B
  N8: Part1.D8_PWM, M1.D
  GND: Part1.GND, RHT1.GND_2, hc-sr1.GND, U1.2, Part2.GND, LCD1.LED+, J1.gnd
  VCC: Part1.VIN, RHT1.Vcc, hc-sr1.VCC, U1.1, Part2.VCC, LCD1.LED-, J1.vcc
  N9: Part1.D22, RHT1.Data-signal
  N10: Part1.D25, U1.5, J1.pulse
  N11: M2.pin_1, U1.10
  N12: M2.pin_2, U1.9
  N13: BAT1.V+, Power_plug1.GND
  N14: BAT1.V-, Power_plug1.VCC

notes:
  Stepper Mototr (Shades)
  DC Water pump
  Micro Servo
  Ultrasonic Sensor
  DH11 Sensor
  Arduino Mega
  I2C LCD Screen
  External PowerSupply
